# Fritzing sketch Robot (saved by Fritzing 0.9.3b)
breadboards: 1

parts:
  Raspberry_Pi_1 = Raspberry Pi 3 [part_number=RPI-3-V1.2]
  M1 = DC Motor  # not connected
  M2 = DC Motor

nets:
  N1: Raspberry_Pi_1.5V, M2.pin_1
